# Fritzing sketch Untitled Sketch (saved by Fritzing 0.9.3b)
breadboards: 1

parts:
  Raspberry_Pi_1 = Raspberry Pi 3 [part_number=RPI-3-V1.2]
  Componente1 = sensor_biometrico
  Componente2 = DeuLigne 1.1 - The Snootlab's LCD shield for Arduino
  R1 = Resistor [tolerance=±5% resistance=220 package=THT]

nets:
  3V3: Raspberry_Pi_1.3v3, Raspberry_Pi_1.3V3, Componente1.VCC, Componente2.+3V3
  N1: Raspberry_Pi_1.GIPO4, Componente1.TX
  N2: Raspberry_Pi_1.GIPO10, Componente1.RX
  N3: Raspberry_Pi_1.GIPO5, Componente2.A0
  N4: Raspberry_Pi_1.GIPO6, Componente2.A1
  N5: Raspberry_Pi_1.GIPO13, Componente2.A2
  N6: Raspberry_Pi_1.GIPO19, Componente2.A3
  GND: Raspberry_Pi_1.GND, Componente1.GND, R1.Pin_0
  N7: Raspberry_Pi_1.GIPO25, Componente2.A4(SDA)
  N8: Raspberry_Pi_1.GIPO24, Componente2.A5(CLK)
  5V: Raspberry_Pi_1.5V, Componente2.+5V
  N9: Componente2.GND, R1.Pin_1

custom parts:
  sensor_biometrico: Adafruit Optical Fingerprint Sensor
